// Logisim project minirv.circ as structural Verilog: 1 circuit, main circuit main
module main (
);

  wire and_1_out, and_2_out, clock_1_out, comparator_1_lt, comparator_2_lt, comparator_3_eq, comparator_4_eq,
       comparator_5_eq, comparator_6_eq, comparator_7_eq, comparator_8_lt, comparator_9_eq, comparator_10_eq,
       d_ff_1_qn, decoder_1_out1, decoder_1_out2, decoder_1_out3, decoder_1_out4, decoder_1_out5,
       decoder_1_out6, decoder_1_out7, decoder_1_out8, decoder_1_out9, decoder_1_out10, decoder_1_out11,
       decoder_1_out12, decoder_1_out13, decoder_1_out14, decoder_1_out15, decoder_1_out16, decoder_1_out17,
       decoder_1_out18, decoder_1_out19, decoder_1_out20, decoder_1_out21, decoder_1_out22, decoder_1_out23,
       decoder_1_out24, decoder_1_out25, decoder_1_out26, decoder_1_out27, decoder_1_out28, decoder_1_out29,
       decoder_1_out30, decoder_1_out31, not_1_out, not_2_out, not_3_out, rgb_video_1_p1, rgb_video_1_p2;
  wire [0:0] d_ff_2_q;
  wire [1:0] adder_3_out_2;
  wire [4:0] and_4_out, bit_extender_1_out;
  wire [7:0] multiplexer_1_out, multiplexer_2_out, multiplexer_3_out, multiplexer_4_out, ram_1_dout,
       ram_1_dout_2, ram_1_dout_3, ram_1_dout_4, rgb_video_1_p6;
  wire [11:0] multiplexer_9_out;
  wire [12:0] pla_1_out;
  wire [23:0] multiplexer_5_out, rgb_video_1_p6_2, shifter_2_out;
  wire [29:0] adder_3_out;
  wire [31:0] adder_1_out, adder_2_out, bit_extender_2_out, multiplexer_6_out, multiplexer_7_out,
       multiplexer_8_out, multiplexer_10_out, multiplexer_11_out, multiplexer_12_out, multiplexer_14_out,
       register_1_q, register_2_q, register_3_q, register_4_q, register_5_q, register_6_q, register_7_q,
       register_8_q, register_9_q, register_10_q, register_11_q, register_12_q, register_13_q, register_14_q,
       register_15_q, register_16_q, register_17_q, register_18_q, register_19_q, register_20_q,
       register_21_q, register_22_q, register_23_q, register_24_q, register_25_q, register_26_q,
       register_27_q, register_28_q, register_29_q, register_30_q, register_31_q, register_32_q,
       register_33_q, register_34_q, shifter_1_out, shifter_3_out;

  and and_1 (and_1_out, comparator_1_lt, pla_1_out[0], comparator_7_eq, not_1_out);
  // Probe on {rgb_video_1_p6_2, rgb_video_1_p6}
  D_Flip_Flop d_ff_1 (.D(and_1_out), .clk(rgb_video_1_p2), .Qn(d_ff_1_qn), .reset(rgb_video_1_p1));  // open: Q, preset
  Comparator #(.mode("unsigned"), .width(32)) comparator_1 (
    .a({adder_3_out, adder_3_out_2}), .b(32'h20040000), .lt(comparator_1_lt));  // open: gt, eq
  Comparator #(.mode("unsigned"), .width(32)) comparator_2 (
    .a({adder_3_out, adder_3_out_2}), .b(32'h20000000), .lt(comparator_2_lt));  // open: gt, eq
  not not_1 (not_1_out, comparator_2_lt);
  // Probe on {adder_3_out, adder_3_out_2}
  not not_2 (not_2_out, and_1_out);
  Multiplexer #(.width(8)) multiplexer_1 (
    .in0(ram_1_dout), .in1(rgb_video_1_p6), .out(multiplexer_1_out), .sel(comparator_3_eq));
  Comparator #(.mode("unsigned"), .width(2)) comparator_3 (
    .a(adder_3_out_2), .b(2'b00), .eq(comparator_3_eq));  // open: gt, lt
  Multiplexer #(.width(8)) multiplexer_2 (
    .in0(ram_1_dout_2), .in1(rgb_video_1_p6), .out(multiplexer_2_out), .sel(comparator_4_eq));
  Comparator #(.mode("unsigned"), .width(2)) comparator_4 (
    .a(adder_3_out_2), .b(2'b01), .eq(comparator_4_eq));  // open: gt, lt
  Multiplexer #(.width(8)) multiplexer_3 (
    .in0(ram_1_dout_3), .in1(rgb_video_1_p6), .out(multiplexer_3_out), .sel(comparator_5_eq));
  Comparator #(.mode("unsigned"), .width(2)) comparator_5 (
    .a(adder_3_out_2), .b(2'b10), .eq(comparator_5_eq));  // open: gt, lt
  Multiplexer #(.width(8)) multiplexer_4 (
    .in0(ram_1_dout_4), .in1(rgb_video_1_p6), .out(multiplexer_4_out), .sel(comparator_6_eq));
  Comparator #(.mode("unsigned"), .width(2)) comparator_6 (
    .a(adder_3_out_2), .b(2'b11), .eq(comparator_6_eq));  // open: gt, lt
  Register #(.width(32)) register_1 (
    .D(adder_1_out), .en(1'b1), .clk(rgb_video_1_p2), .Q(register_1_q), .clr(rgb_video_1_p1));
  Clock clock_1 (.out(clock_1_out));
  // Probe on shifter_2_out
  Shifter #(.shift("lr"), .width(32)) shifter_1 (
    .in({adder_3_out, adder_3_out_2}), .\dist (5'b00010), .out(shifter_1_out));
  and and_2 (and_2_out, not_2_out, pla_1_out[0]);
  Comparator #(.mode("unsigned"), .width(3)) comparator_7 (
    .a(multiplexer_8_out[14:12]), .b(3'b010), .eq(comparator_7_eq));  // open: gt, lt
  // RGB_Video #(.cursor("No Cursor"), .height(256), .scale(1), .width(256)) rgb_video_1: pin names not known; wires that end beside it: rgb_video_1_p1, rgb_video_1_p2, and_1_out, shifter_1_out[7:0], shifter_1_out[15:8], {rgb_video_1_p6_2[15:0], rgb_video_1_p6}
  and and_3 (rgb_video_1_p2, comparator_8_lt, not_3_out, d_ff_1_qn, clock_1_out);
  Multiplexer #(.width(24)) multiplexer_5 (
    .in0(shifter_2_out), .in1(shifter_1_out[23:0]), .out(multiplexer_5_out), .sel(pla_1_out[2]));
  Multiplexer #(.width(32)) multiplexer_6 (
    .in0({multiplexer_4_out, multiplexer_3_out, multiplexer_2_out, multiplexer_1_out}),
    .in1({rgb_video_1_p6_2, rgb_video_1_p6}), .out(multiplexer_6_out), .sel(comparator_7_eq));
  Adder #(.width(32)) adder_1 (.a(register_1_q), .b(32'h1), .out(adder_1_out), .cin(1'b0));  // open: cout
  Comparator #(.mode("unsigned"), .width(32)) comparator_8 (
    .a(register_1_q), .b({32{1'b1}}), .lt(comparator_8_lt));  // open: gt, eq
  // Probe on multiplexer_6_out
  // Probe on multiplexer_8_out[14:12]
  POR por_1 (.out(rgb_video_1_p1));
  // Probe on multiplexer_7_out
  RAM #(.addrWidth(24), .asyncread("true"), .dataWidth(32), .\type ("nonvolatile")) ram_1 (
    .addr(multiplexer_5_out), .we(and_2_out), .oe(1'b1), .clk(rgb_video_1_p2), .din(multiplexer_6_out),
    .dout({ram_1_dout_4, ram_1_dout_3, ram_1_dout_2, ram_1_dout}));
  // Probe on multiplexer_5_out
  Comparator #(.mode("unsigned"), .width(32)) comparator_9 (
    .a(32'hfffffff), .b(register_2_q), .eq(comparator_9_eq));  // open: gt, lt
  Register #(.width(32)) register_2 (
    .D(multiplexer_7_out), .en(pla_1_out[10]), .clk(rgb_video_1_p2), .Q(register_2_q), .clr(rgb_video_1_p1));
  not not_3 (not_3_out, comparator_9_eq);
  Adder #(.width(32)) adder_2 (.a(register_2_q), .b(32'h4), .out(adder_2_out), .cin(1'b0));  // open: cout
  // Probe on {ram_1_dout_4, ram_1_dout_3, ram_1_dout_2, ram_1_dout}
  Register #(.width(32)) register_3 (
    .D({ram_1_dout_4, ram_1_dout_3, ram_1_dout_2, ram_1_dout}), .en(pla_1_out[3]), .clk(rgb_video_1_p2),
    .Q(register_3_q), .clr(rgb_video_1_p1));
  Shifter #(.shift("lr"), .width(24)) shifter_2 (.in(register_2_q[23:0]), .\dist (5'b00010), .out(shifter_2_out));
  Multiplexer #(.width(32)) multiplexer_7 (
    .in0(adder_2_out), .in1({adder_3_out, adder_3_out_2}), .out(multiplexer_7_out), .sel(pla_1_out[12]));
  // Probe on multiplexer_8_out
  Multiplexer #(.width(32)) multiplexer_8 (
    .in0({ram_1_dout_4, ram_1_dout_3, ram_1_dout_2, ram_1_dout}), .in1(register_3_q),
    .out(multiplexer_8_out), .sel(pla_1_out[4]));
  // Probe on multiplexer_8_out[6:0]
  // Probe on multiplexer_8_out[31:20]
  D_Flip_Flop d_ff_2 (
    .D(pla_1_out[3]), .clk(rgb_video_1_p2), .Q(d_ff_2_q[0]), .reset(rgb_video_1_p1));  // open: Qn, preset
  Multiplexer #(.width(12)) multiplexer_9 (
    .in0(multiplexer_8_out[31:20]), .in1({multiplexer_8_out[31:25], multiplexer_8_out[11:7]}),
    .out(multiplexer_9_out), .sel(pla_1_out[6]));
  // Probe on multiplexer_8_out[11:7]
  assign bit_extender_1_out = {{4{pla_1_out[7]}}, pla_1_out[7]};  // Bit_Extender bit_extender_1
  PLA #(.in_width(6), .out_width(13), .\table ("011010 0011010000010 # LUI\n110010 1010110100010 # JALR\n000000 0100000101010 # LW(H)\n000001 0011110110110 # LW\n010000 0100001101000 # SAVE(H)\n010001 0010001110111 # SAVE\n001000 0010010100010 # ADDI\n011000 0010010000010 # ADD")) pla_1 (
    .in({multiplexer_8_out[6:2], d_ff_2_q[0]}), .out(pla_1_out));
  assign bit_extender_2_out = {{20{multiplexer_9_out[11]}}, multiplexer_9_out};  // Bit_Extender bit_extender_2
  Comparator #(.mode("unsigned"), .width(3)) comparator_10 (
    .a(multiplexer_8_out[14:12]), .b(3'b100), .eq(comparator_10_eq));  // open: gt, lt
  assign and_4_out = multiplexer_8_out[11:7] & bit_extender_1_out;  // AND_Gate and_4, 5 bits wide
  // Probe on {multiplexer_8_out[6:2], d_ff_2_q[0]}
  Shifter #(.shift("lr"), .width(32)) shifter_3 (
    .in({ram_1_dout_4, ram_1_dout_3, ram_1_dout_2, ram_1_dout}), .\dist ({adder_3_out_2, 3'b000}),
    .out(shifter_3_out));
  Decoder #(.disabled("Z"), .enable("false"), .select(5)) decoder_1 (
    .out1(decoder_1_out1), .out2(decoder_1_out2), .out3(decoder_1_out3), .out4(decoder_1_out4),
    .out5(decoder_1_out5), .out6(decoder_1_out6), .out7(decoder_1_out7), .out8(decoder_1_out8),
    .out9(decoder_1_out9), .out10(decoder_1_out10), .out11(decoder_1_out11), .out12(decoder_1_out12),
    .out13(decoder_1_out13), .out14(decoder_1_out14), .out15(decoder_1_out15), .out16(decoder_1_out16),
    .out17(decoder_1_out17), .out18(decoder_1_out18), .out19(decoder_1_out19), .out20(decoder_1_out20),
    .out21(decoder_1_out21), .out22(decoder_1_out22), .out23(decoder_1_out23), .out24(decoder_1_out24),
    .out25(decoder_1_out25), .out26(decoder_1_out26), .out27(decoder_1_out27), .out28(decoder_1_out28),
    .out29(decoder_1_out29), .out30(decoder_1_out30), .out31(decoder_1_out31), .sel(and_4_out));  // open: out0
  Multiplexer #(.width(32)) multiplexer_10 (
    .in0({ram_1_dout_4, ram_1_dout_3, ram_1_dout_2, ram_1_dout}), .in1({{24{1'b0}}, shifter_3_out[7:0]}),
    .out(multiplexer_10_out), .sel(comparator_10_eq));
  // Probe on multiplexer_11_out
  Multiplexer #(.select(2), .width(32)) multiplexer_11 (
    .in0({adder_3_out, adder_3_out_2}), .in1(adder_2_out),
    .in2({ram_1_dout_4, ram_1_dout_3, ram_1_dout_2[7:4], {12{1'b0}}}), .in3(multiplexer_10_out),
    .out(multiplexer_11_out), .sel(pla_1_out[9:8]));
  // Probe on pla_1_out[9:8]
  Register #(.width(32)) register_4 (
    .D(multiplexer_11_out), .en(decoder_1_out8), .clk(rgb_video_1_p2), .Q(register_4_q), .clr(rgb_video_1_p1));
  Register #(.width(32)) register_5 (
    .D(multiplexer_11_out), .en(decoder_1_out16), .clk(rgb_video_1_p2), .Q(register_5_q), .clr(rgb_video_1_p1));
  Register #(.width(32)) register_6 (
    .D(multiplexer_11_out), .en(decoder_1_out24), .clk(rgb_video_1_p2), .Q(register_6_q), .clr(rgb_video_1_p1));
  Register #(.width(32)) register_7 (
    .D(multiplexer_11_out), .en(decoder_1_out1), .clk(rgb_video_1_p2), .Q(register_7_q), .clr(rgb_video_1_p1));
  Register #(.width(32)) register_8 (
    .D(multiplexer_11_out), .en(decoder_1_out9), .clk(rgb_video_1_p2), .Q(register_8_q), .clr(rgb_video_1_p1));
  Register #(.width(32)) register_9 (
    .D(multiplexer_11_out), .en(decoder_1_out17), .clk(rgb_video_1_p2), .Q(register_9_q), .clr(rgb_video_1_p1));
  Register #(.width(32)) register_10 (
    .D(multiplexer_11_out), .en(decoder_1_out25), .clk(rgb_video_1_p2), .Q(register_10_q),
    .clr(rgb_video_1_p1));
  Register #(.width(32)) register_11 (
    .D(multiplexer_11_out), .en(decoder_1_out2), .clk(rgb_video_1_p2), .Q(register_11_q), .clr(rgb_video_1_p1));
  Register #(.width(32)) register_12 (
    .D(multiplexer_11_out), .en(decoder_1_out10), .clk(rgb_video_1_p2), .Q(register_12_q),
    .clr(rgb_video_1_p1));
  Register #(.width(32)) register_13 (
    .D(multiplexer_11_out), .en(decoder_1_out18), .clk(rgb_video_1_p2), .Q(register_13_q),
    .clr(rgb_video_1_p1));
  Register #(.width(32)) register_14 (
    .D(multiplexer_11_out), .en(decoder_1_out26), .clk(rgb_video_1_p2), .Q(register_14_q),
    .clr(rgb_video_1_p1));
  Register #(.width(32)) register_15 (
    .D(multiplexer_11_out), .en(decoder_1_out3), .clk(rgb_video_1_p2), .Q(register_15_q), .clr(rgb_video_1_p1));
  Register #(.width(32)) register_16 (
    .D(multiplexer_11_out), .en(decoder_1_out11), .clk(rgb_video_1_p2), .Q(register_16_q),
    .clr(rgb_video_1_p1));
  Register #(.width(32)) register_17 (
    .D(multiplexer_11_out), .en(decoder_1_out19), .clk(rgb_video_1_p2), .Q(register_17_q),
    .clr(rgb_video_1_p1));
  Register #(.width(32)) register_18 (
    .D(multiplexer_11_out), .en(decoder_1_out27), .clk(rgb_video_1_p2), .Q(register_18_q),
    .clr(rgb_video_1_p1));
  Register #(.width(32)) register_19 (
    .D(multiplexer_11_out), .en(decoder_1_out4), .clk(rgb_video_1_p2), .Q(register_19_q), .clr(rgb_video_1_p1));
  Register #(.width(32)) register_20 (
    .D(multiplexer_11_out), .en(decoder_1_out12), .clk(rgb_video_1_p2), .Q(register_20_q),
    .clr(rgb_video_1_p1));
  Register #(.width(32)) register_21 (
    .D(multiplexer_11_out), .en(decoder_1_out20), .clk(rgb_video_1_p2), .Q(register_21_q),
    .clr(rgb_video_1_p1));
  Register #(.width(32)) register_22 (
    .D(multiplexer_11_out), .en(decoder_1_out28), .clk(rgb_video_1_p2), .Q(register_22_q),
    .clr(rgb_video_1_p1));
  Register #(.width(32)) register_23 (
    .D(multiplexer_11_out), .en(decoder_1_out5), .clk(rgb_video_1_p2), .Q(register_23_q), .clr(rgb_video_1_p1));
  Register #(.width(32)) register_24 (
    .D(multiplexer_11_out), .en(decoder_1_out13), .clk(rgb_video_1_p2), .Q(register_24_q),
    .clr(rgb_video_1_p1));
  Register #(.width(32)) register_25 (
    .D(multiplexer_11_out), .en(decoder_1_out21), .clk(rgb_video_1_p2), .Q(register_25_q),
    .clr(rgb_video_1_p1));
  Register #(.width(32)) register_26 (
    .D(multiplexer_11_out), .en(decoder_1_out29), .clk(rgb_video_1_p2), .Q(register_26_q),
    .clr(rgb_video_1_p1));
  Register #(.width(32)) register_27 (
    .D(multiplexer_11_out), .en(decoder_1_out6), .clk(rgb_video_1_p2), .Q(register_27_q), .clr(rgb_video_1_p1));
  Register #(.width(32)) register_28 (
    .D(multiplexer_11_out), .en(decoder_1_out14), .clk(rgb_video_1_p2), .Q(register_28_q),
    .clr(rgb_video_1_p1));
  Register #(.width(32)) register_29 (
    .D(multiplexer_11_out), .en(decoder_1_out22), .clk(rgb_video_1_p2), .Q(register_29_q),
    .clr(rgb_video_1_p1));
  Register #(.width(32)) register_30 (
    .D(multiplexer_11_out), .en(decoder_1_out30), .clk(rgb_video_1_p2), .Q(register_30_q),
    .clr(rgb_video_1_p1));
  Register #(.width(32)) register_31 (
    .D(multiplexer_11_out), .en(decoder_1_out7), .clk(rgb_video_1_p2), .Q(register_31_q), .clr(rgb_video_1_p1));
  Register #(.width(32)) register_32 (
    .D(multiplexer_11_out), .en(decoder_1_out15), .clk(rgb_video_1_p2), .Q(register_32_q),
    .clr(rgb_video_1_p1));
  Register #(.width(32)) register_33 (
    .D(multiplexer_11_out), .en(decoder_1_out23), .clk(rgb_video_1_p2), .Q(register_33_q),
    .clr(rgb_video_1_p1));
  Register #(.width(32)) register_34 (
    .D(multiplexer_11_out), .en(decoder_1_out31), .clk(rgb_video_1_p2), .Q(register_34_q),
    .clr(rgb_video_1_p1));
  // Probe on multiplexer_8_out[19:15]
  // Probe on multiplexer_8_out[24:20]
  Multiplexer #(.select(5), .width(32)) multiplexer_12 (
    .in0({32{1'b0}}), .in1(register_7_q), .in2(register_11_q), .in3(register_15_q), .in4(register_19_q),
    .in5(register_23_q), .in6(register_27_q), .in7(register_31_q), .in8(register_4_q), .in9(register_8_q),
    .in10(register_12_q), .in11(register_16_q), .in12(register_20_q), .in13(register_24_q),
    .in14(register_28_q), .in15(register_32_q), .in16(register_5_q), .in17(register_9_q),
    .in18(register_13_q), .in19(register_17_q), .in20(register_21_q), .in21(register_25_q),
    .in22(register_29_q), .in23(register_33_q), .in24(register_6_q), .in25(register_10_q),
    .in26(register_14_q), .in27(register_18_q), .in28(register_22_q), .in29(register_26_q),
    .in30(register_30_q), .in31(register_34_q), .out(multiplexer_12_out), .sel(multiplexer_8_out[19:15]));
  Multiplexer #(.select(5), .width(32)) multiplexer_13 (
    .in0({32{1'b0}}), .in1(register_7_q), .in2(register_11_q), .in3(register_15_q), .in4(register_19_q),
    .in5(register_23_q), .in6(register_27_q), .in7(register_31_q), .in8(register_4_q), .in9(register_8_q),
    .in10(register_12_q), .in11(register_16_q), .in12(register_20_q), .in13(register_24_q),
    .in14(register_28_q), .in15(register_32_q), .in16(register_5_q), .in17(register_9_q),
    .in18(register_13_q), .in19(register_17_q), .in20(register_21_q), .in21(register_25_q),
    .in22(register_29_q), .in23(register_33_q), .in24(register_6_q), .in25(register_10_q),
    .in26(register_14_q), .in27(register_18_q), .in28(register_22_q), .in29(register_26_q),
    .in30(register_30_q), .in31(register_34_q), .out({rgb_video_1_p6_2, rgb_video_1_p6}),
    .sel(multiplexer_8_out[24:20]));
  // Probe on {rgb_video_1_p6_2, rgb_video_1_p6}
  Multiplexer #(.width(32)) multiplexer_14 (
    .in0({rgb_video_1_p6_2, rgb_video_1_p6}), .in1(bit_extender_2_out), .out(multiplexer_14_out),
    .sel(pla_1_out[5]));
  // Probe on pla_1_out[5]
  // Probe on multiplexer_12_out
  // Probe on multiplexer_14_out
  Adder #(.width(32)) adder_3 (
    .a(multiplexer_12_out), .b(multiplexer_14_out), .out({adder_3_out, adder_3_out_2}), .cin(1'b0));  // open: cout
  // Probe on {adder_3_out, adder_3_out_2}
endmodule
